// Logisim project emergency alarm system.circ as structural Verilog: 1 circuit, main circuit main
module main (
  input  in_1,
  input  H_heat,
  input  M_manual,
  output A_alarm
);

  wire and_1_out;

  and and_1 (and_1_out, in_1, H_heat);
  or or_1 (A_alarm, and_1_out, M_manual);

  // Notes on the sheet:
  //   S-smoke
endmodule
