// Logisim project full adder.circ as structural Verilog: 1 circuit, main circuit main
module main (
  input  A,
  input  B,
  input  Cin,
  output SUM,
  output CARRY
);

  wire AND_2_out, AND_out, XOR_out;

  xor XOR (XOR_out, A, B);
  and AND (AND_out, B, A);
  xor XOR_2 (SUM, XOR_out, Cin);
  and AND_2 (AND_2_out, Cin, XOR_out);
  xor XOR_3 (CARRY, AND_2_out, AND_out);

  // Notes on the sheet:
  //   carry
endmodule
