// Logisim project smart locker.circ as structural Verilog: 1 circuit, main circuit main
module main (
  input  door,
  input  window,
  input  motioin,
  output Y__Alarm
);

  or or_1 (Y__Alarm, door, window, motioin);

  // Notes on the sheet:
  //   A-
  //   B-
  //   C-
endmodule
